// Logisim project G2 copy.circ as structural Verilog: 2 circuits, main circuit main
module main (
  input  in_1,
  output [31:0] out_2,
  output [31:0] out_3,
  output [31:0] out_4,
  output [31:0] out_5,
  output [31:0] out_6,
  output [5:0] OP_code,
  output out_8,
  output [31:0] out_9,
  output out_10,
  output [4:0] out_11,
  output [4:0] out_12,
  output [31:0] out_13,
  output [2:0] out_14,
  output [15:0] out_15,
  output [3:0] out_16,
  output [4:0] out_17,
  output [5:0] out_18
);

  wire ALUOp_jump, ALUSrc, Branch, clock_1_out, clock_2_out, clock_3_out, Jump, MemRead, MemtoReg, MemWrite,
       not_1_out, not_2_out, not_3_out, or_1_out, RegDst, RegWrite;
  wire [4:0] multiplexer_1_out;
  wire [31:0] adder_1_p3, bit_extender_2_out, mips_alu_1_p5, mips_ram_1_p6, multiplexer_5_out,
       multiplexer_6_out, PC_q;

  Register #(.width(32)) PC (.D(multiplexer_6_out), .Q(PC_q), .clk(clock_1_out), .clr(in_1));  // open: en
  Clock clock_1 (.out(clock_1_out));
  // Adder adder_1: pin names not known; wires that end beside it: PC_q, 32'h4, adder_1_p3
  // MIPSProgramROM mipsprogramrom_1: pin names not known; wires that end beside it: PC_q, {OP_code, out_9[25:0]}
  // PLA Control: pin names not known; wires that end beside it: OP_code
  Multiplexer #(.width(5), .enable("false")) multiplexer_1 (
    .in0(out_9[20:16]), .in1(out_9[15:11]), .out(multiplexer_1_out), .sel(RegDst));
  assign out_2 = {{6{1'b0}}, out_9[25:0]};  // Bit_Extender bit_extender_1
  not not_1 (not_1_out, Jump);
  Multiplexer #(.width(32), .enable("false")) multiplexer_2 (
    .in0(adder_1_p3), .in1(out_6), .out(out_3), .sel(not_1_out));
  Clock clock_2 (.out(clock_2_out));
  Multiplexer #(.width(5), .enable("false")) multiplexer_3 (
    .in0({5{1'b1}}), .in1(multiplexer_1_out), .out(out_17), .sel(not_1_out));
  assign bit_extender_2_out = {{16{1'b0}}, out_9[15:0]};  // Bit_Extender bit_extender_2
  // RegisterFile registerfile_1: pin names not known; wires that end beside it: out_3, clock_2_out, RegWrite, out_17, out_9[25:21], out_9[20:16], in_1, out_4, out_13, out_13
  Multiplexer #(.width(32), .enable("false")) multiplexer_4 (
    .in0(out_13), .in1(bit_extender_2_out), .out(out_5), .sel(ALUSrc));
  Multiplexer #(.width(32), .enable("false")) multiplexer_5 (
    .in0(adder_1_p3), .in1(out_4), .out(multiplexer_5_out), .sel(or_1_out));
  or or_1 (or_1_out, Jump, ALUOp_jump);
  // MIPS_ALU mips_alu_1: pin names not known; wires that end beside it: out_4, out_5, out_16, out_8, mips_alu_1_p5, out_10, out_13
  ALUOp ALUOp (.ALUOp(out_14), .funct(out_9[5:0]), .ALU(out_16), .JUMP(ALUOp_jump));
  Multiplexer #(.width(32), .enable("false")) multiplexer_6 (
    .in0(out_2), .in1(multiplexer_5_out), .out(multiplexer_6_out), .sel(not_2_out));
  not not_2 (not_2_out, Branch);
  not not_3 (not_3_out, clock_3_out);
  Clock clock_3 (.out(clock_3_out));
  // MIPS_RAM mips_ram_1: pin names not known; wires that end beside it: mips_alu_1_p5[23:0], MemWrite, MemRead, not_3_out, in_1, mips_ram_1_p6
  Multiplexer #(.width(32), .enable("false")) multiplexer_7 (
    .in0(mips_ram_1_p6), .in1(mips_alu_1_p5), .out(out_6), .sel(MemtoReg));
  // MIPSProgramROM mipsprogramrom_2: pin names not known

  assign out_9[31:26] = OP_code;
  assign out_11 = out_9[20:16];
  assign out_12 = out_9[25:21];
  assign out_15 = out_9[15:0];
  assign out_18 = out_9[5:0];

  // Other names for the same wires on the sheet: ALUOp[2:0] = out_14; Clear = in_1
endmodule

module ALUOp (
  input  [2:0] ALUOp,
  input  [5:0] funct,
  output [3:0] ALU,
  output JUMP
);

  // PLA pla_1: pin names not known; wires that end beside it: {ALUOp, funct}
endmodule
