// Logisim project G2.circ as structural Verilog: 13 circuits, main circuit main
module main (
  input  in_1,
  output out_2,
  output out_3,
  output out_4,
  output out_5
);

  wire ALUjump, ALUSrc, and_1_out, Branch, clock_1_out, clock_2_out, clock_3_out, clock_4_out, clock_5_out,
       clock_6_out, clock_7_out, clock_8_out, data_hazard_1_alert_rs, data_hazard_1_alert_rt,
       data_hazard_2_alert_rs, data_hazard_2_alert_rt, data_hazard_3_alert_rs, data_hazard_3_alert_rt,
       Hazard, is_lw_1_type, is_lw_2_type, jal, MemRead, MemtoReg, MemWrite, mips_ram_1_p5, nor_1_out,
       not_1_out, not_2_out, not_3_out, not_5_out, or_2_out, RegDst, RegWrite, stall, state_1_memtoreg,
       state_1_memtoreg_2, state_1_memtoreg_out, state_1_memtoreg_out_2, state_1_memtoreg_out_3,
       state_1_memtoreg_out_4, state_1_memtoreg_out_5, state_2_memtoreg, state_2_memtoreg_2,
       state_2_memtoreg_out, state_2_memtoreg_out_2, state_2_memtoreg_out_5, state_3_memtoreg_out, undriven,
       wait_1_cycle_1_out_2, wait_1_cycle_2_out_2, WriteEnable, WriteTo_RA;
  wire [0:0] Control_p2;
  wire [1:0] check_type_1_type, forwarding_unit_1_out_4, forwarding_unit_2_out_4;
  wire [2:0] ALUOp, state_1_regwrite_out_2;
  wire [3:0] ALUOp_alu;
  wire [4:0] multiplexer_3_out, multiplexer_4_out, rd_EX, rd_MEM, rd_WB;
  wire [5:0] Control, id_ex_1_aluop_out, if_id_1_instruction_out;
  wire [25:6] if_id_1_instruction_out_2;
  wire [31:0] adder_1_p3, adder_2_p3, bit_extender_1_out, ex_mem_1_alu_result_out, ex_mem_1_read_data_2_2,
       EXResult, id_ex_1_pc_out, id_ex_1_read_data_1_out, id_ex_1_read_data_2_out, id_ex_1_sign_ext_out,
       if_id_1_pc_out, jal_pc_1_out_3, mem_wb_1_alu_result_out, mem_wb_1_memout_out, MEMResult,
       mips_alu_1_p6, mips_alu_2_p4, mips_ram_1_p7, mipsprogramrom_1_p2, multiplexer_1_out,
       multiplexer_2_out, multiplexer_5_out, multiplexer_6_out, multiplexer_7_out, multiplexer_8_out,
       multiplexer_9_out, multiplexer_10_out, PC_q, registerfile_1_p8, registerfile_1_p9, shifter_1_out,
       state_1_memtoreg_out_6, state_2_memtoreg_out_6, WBResult;

  Register #(.width(32)) PC (.D(multiplexer_2_out), .Q(PC_q), .clk(clock_1_out), .clr(in_1));  // open: en
  Clock clock_1 (.out(clock_1_out));
  // Adder adder_1: pin names not known; wires that end beside it: PC_q, 32'h4, adder_1_p3
  Multiplexer #(.width(32), .enable("false")) multiplexer_1 (
    .in0(adder_1_p3), .in1(PC_q), .out(multiplexer_1_out), .sel(stall));
  Multiplexer #(.width(32), .enable("false")) multiplexer_2 (
    .in0(multiplexer_10_out), .in1(multiplexer_1_out), .out(multiplexer_2_out), .sel(nor_1_out));
  Clock clock_2 (.out(clock_2_out));
  not not_1 (not_1_out, nor_1_out);
  // MIPSProgramROM mipsprogramrom_1: pin names not known; wires that end beside it: PC_q, mipsprogramrom_1_p2
  D_Flip_Flop #(.trigger("falling")) d_ff_1 (
    .clk(clock_2_out), .D(not_1_out), .Q(out_2), .Qn(out_3), .en(1'b1), .reset(1'b0));  // open: preset
  nor nor_1 (nor_1_out, state_1_memtoreg_out_4, state_1_memtoreg_out_5, ALUjump);
  IF_ID if_id_1 (
    .Clock(clock_3_out), .PC_in(multiplexer_1_out), .Instruction_in(mipsprogramrom_1_p2),
    .PC_out(if_id_1_pc_out), .Instruction_out({Control, if_id_1_instruction_out_2, if_id_1_instruction_out}),
    .Clear(1'b0));
  Clock clock_3 (.out(clock_3_out));
  Check_type check_type_1 (.OP(Control), .\type (check_type_1_type));
  Data_Hazard data_hazard_1 (
    .rt(if_id_1_instruction_out_2[20:16]), .rd(rd_EX), .rs(if_id_1_instruction_out_2[25:21]),
    .\type (check_type_1_type), .Alert_rt(data_hazard_1_alert_rt), .Alert_rs(data_hazard_1_alert_rs));
  Data_Hazard data_hazard_2 (
    .rt(if_id_1_instruction_out_2[20:16]), .rd(rd_MEM), .rs(if_id_1_instruction_out_2[25:21]),
    .\type (check_type_1_type), .Alert_rt(data_hazard_2_alert_rt), .Alert_rs(data_hazard_2_alert_rs));
  Data_Hazard data_hazard_3 (
    .rt(if_id_1_instruction_out_2[20:16]), .rd(rd_WB), .rs(if_id_1_instruction_out_2[25:21]),
    .\type (check_type_1_type), .Alert_rt(data_hazard_3_alert_rt), .Alert_rs(data_hazard_3_alert_rs));
  Multiplexer #(.width(5), .enable("false")) multiplexer_3 (
    .in0(if_id_1_instruction_out_2[20:16]), .in1(if_id_1_instruction_out_2[15:11]), .out(multiplexer_3_out),
    .sel(RegDst));
  // PLA Control: pin names not known; wires that end beside it: Control, Control_p2[0]
  Forwarding_unit forwarding_unit_1 (
    .in_1(data_hazard_1_alert_rs), .in_2(data_hazard_2_alert_rs), .in_3(data_hazard_3_alert_rs),
    .out_4(forwarding_unit_1_out_4));
  or or_1 (Hazard, data_hazard_1_alert_rs, data_hazard_2_alert_rs, data_hazard_3_alert_rs, data_hazard_1_alert_rt, data_hazard_2_alert_rt, data_hazard_3_alert_rt);
  Forwarding_unit forwarding_unit_2 (
    .in_1(data_hazard_1_alert_rt), .in_2(data_hazard_2_alert_rt), .in_3(data_hazard_3_alert_rt),
    .out_4(forwarding_unit_2_out_4));
  Clock clock_4 (.out(clock_4_out));
  Multiplexer #(.width(5), .enable("false")) multiplexer_4 (
    .in0(rd_WB), .in1({5{1'b1}}), .out(multiplexer_4_out), .sel(WriteTo_RA));
  assign bit_extender_1_out = {{16{1'b0}}, {if_id_1_instruction_out_2[15:6], if_id_1_instruction_out}};  // Bit_Extender bit_extender_1
  // RegisterFile registerfile_1: pin names not known; wires that end beside it: WBResult, clock_4_out, WriteEnable, multiplexer_4_out, if_id_1_instruction_out_2[25:21], if_id_1_instruction_out_2[20:16], in_1, registerfile_1_p8, registerfile_1_p9
  Wait_1_cycle wait_1_cycle_1 (.Trigger_stall(stall), .out_2(wait_1_cycle_1_out_2));
  ID_EX id_ex_1 (
    .Clock(clock_5_out), .PC_in(if_id_1_pc_out), .Read_Data_1_in(multiplexer_5_out),
    .Read_Data_2_in(multiplexer_6_out), .Sign_Ext_in(bit_extender_1_out), .PC_out(id_ex_1_pc_out),
    .Read_Data_1_out(id_ex_1_read_data_1_out), .Read_Data_2_out(id_ex_1_read_data_2_out),
    .Sign_Ext_out(id_ex_1_sign_ext_out), .ALUOp_in(if_id_1_instruction_out), .ALUOp_out(id_ex_1_aluop_out),
    .Disable_output(wait_1_cycle_1_out_2));  // open: Clear
  Multiplexer #(.select(2), .width(32), .enable("false")) multiplexer_5 (
    .in0(registerfile_1_p8), .in1(EXResult), .in2(MEMResult), .in3(WBResult), .out(multiplexer_5_out),
    .sel(forwarding_unit_2_out_4));
  Multiplexer #(.select(2), .width(32), .enable("false")) multiplexer_6 (
    .in0(registerfile_1_p9), .in1(EXResult), .in2(MEMResult), .in3(WBResult), .out(multiplexer_6_out),
    .sel(forwarding_unit_1_out_4));
  Clock clock_5 (.out(clock_5_out));
  State state_1 (
    .Clock(clock_5_out), .RegWrite_in(multiplexer_3_out), .MemToReg_in(RegWrite), .MemToReg_in_2(MemtoReg),
    .RegWrite_out(rd_EX), .MemToReg(state_1_memtoreg), .MemToReg_out(state_1_memtoreg_out),
    .MemToReg_in_3(MemRead), .MemToReg_2(state_1_memtoreg_2), .MemToReg_in_4(MemWrite),
    .MemToReg_out_2(state_1_memtoreg_out_2), .MemToReg_in_5(ALUSrc), .MemToReg_out_3(state_1_memtoreg_out_3),
    .RegWrite_in_2(ALUOp), .RegWrite_out_2(state_1_regwrite_out_2), .MemToReg_in_6(Branch),
    .MemToReg_out_4(state_1_memtoreg_out_4), .MemToReg_in_7(jal), .MemToReg_out_5(state_1_memtoreg_out_5),
    .MemToReg_in_8({Control, if_id_1_instruction_out_2, if_id_1_instruction_out}),
    .MemToReg_out_6(state_1_memtoreg_out_6), .Clear(1'b0), .in_3(wait_1_cycle_2_out_2));  // open: RegWrite_in_3, RegWrite_out_3, RegWrite_in_4, RegWrite_out_4
  Wait_1_cycle wait_1_cycle_2 (.Trigger_stall(stall), .out_2(wait_1_cycle_2_out_2));
  jal_PC jal_pc_1 (.in_1(state_1_memtoreg_out_6), .in_2(id_ex_1_pc_out), .out_3(jal_pc_1_out_3));
  Multiplexer #(.width(32), .enable("false")) multiplexer_7 (
    .in0(id_ex_1_pc_out), .in1(id_ex_1_read_data_1_out), .out(multiplexer_7_out), .sel(ALUjump));
  Shifter #(.width(32)) shifter_1 (.in(id_ex_1_sign_ext_out), .\dist (5'b00010), .out(shifter_1_out));
  Multiplexer #(.width(32), .enable("false")) multiplexer_8 (
    .in0(id_ex_1_read_data_2_out), .in1(id_ex_1_sign_ext_out), .out(multiplexer_8_out),
    .sel(state_1_memtoreg_out_3));
  ALUOp u_ALUOp (.ALUOp(state_1_regwrite_out_2), .funct(id_ex_1_aluop_out), .ALU(ALUOp_alu), .JUMP(ALUjump));
  Multiplexer #(.width(32), .enable("false")) multiplexer_9 (
    .in0(jal_pc_1_out_3), .in1(multiplexer_7_out), .out(multiplexer_9_out), .sel(not_2_out));
  not not_2 (not_2_out, state_1_memtoreg_out_5);
  // MIPS_ALU mips_alu_1: pin names not known; wires that end beside it: id_ex_1_read_data_2_out, id_ex_1_read_data_1_out, multiplexer_8_out, ALUOp_alu, out_4, mips_alu_1_p6, out_5
  // MIPS_ALU mips_alu_2: pin names not known; wires that end beside it: id_ex_1_pc_out, shifter_1_out, 4'b0010, mips_alu_2_p4
  or or_2 (or_2_out, not_3_out, ALUjump);
  not not_3 (not_3_out, and_1_out);
  and and_1 (and_1_out, out_4, state_1_memtoreg_out_4);
  // Adder adder_2: pin names not known; wires that end beside it: id_ex_1_pc_out, 32'h4, adder_2_p3
  Is_lw is_lw_1 (.in_1(state_1_memtoreg_out_6), .\type (is_lw_1_type));
  and and_2 (stall, is_lw_1_type, Hazard);
  Multiplexer #(.width(32), .enable("false")) multiplexer_10 (
    .in0(mips_alu_2_p4), .in1(multiplexer_9_out), .out(multiplexer_10_out), .sel(or_2_out));
  EX_MEM ex_mem_1 (
    .Clock(clock_6_out), .PC_in(multiplexer_10_out), .ALU_result_in(EXResult),
    .Read_Data_2(id_ex_1_read_data_2_out), .ALU_result_out(ex_mem_1_alu_result_out),
    .Read_Data_2_2(ex_mem_1_read_data_2_2));  // open: PC_out
  Multiplexer #(.width(32), .enable("false")) multiplexer_11 (
    .in0(mips_alu_1_p6), .in1(adder_2_p3), .out(EXResult), .sel(state_1_memtoreg_out_5));
  Clock clock_6 (.out(clock_6_out));
  State state_2 (
    .Clock(clock_6_out), .RegWrite_in(rd_EX), .MemToReg_in(state_1_memtoreg),
    .MemToReg_in_2(state_1_memtoreg_out), .RegWrite_out(rd_MEM), .MemToReg(state_2_memtoreg),
    .MemToReg_out(state_2_memtoreg_out), .MemToReg_in_3(state_1_memtoreg_2), .MemToReg_2(state_2_memtoreg_2),
    .MemToReg_in_4(state_1_memtoreg_out_2), .MemToReg_out_2(state_2_memtoreg_out_2),
    .MemToReg_in_7(state_1_memtoreg_out_5), .MemToReg_out_5(state_2_memtoreg_out_5),
    .MemToReg_in_8(state_1_memtoreg_out_6), .MemToReg_out_6(state_2_memtoreg_out_6), .Clear(1'b0), .in_3(1'b0));  // open: MemToReg_in_5, MemToReg_out_3, RegWrite_in_2, RegWrite_out_2, MemToReg_in_6, MemToReg_out_4, RegWrite_in_3, RegWrite_out_3, RegWrite_in_4, RegWrite_out_4
  // MIPS_RAM mips_ram_1: pin names not known; wires that end beside it: ex_mem_1_alu_result_out[23:0], ex_mem_1_read_data_2_2, state_2_memtoreg_out_2, state_2_memtoreg_2, mips_ram_1_p5, in_1, mips_ram_1_p7
  not not_4 (mips_ram_1_p5, clock_7_out);
  Clock clock_7 (.out(clock_7_out));
  Multiplexer #(.width(32), .enable("false")) multiplexer_12 (
    .in0(mips_ram_1_p7), .in1(ex_mem_1_alu_result_out), .out(MEMResult), .sel(not_5_out));
  not not_5 (not_5_out, is_lw_2_type);
  Is_lw is_lw_2 (.in_1(state_2_memtoreg_out_6), .\type (is_lw_2_type));
  MEM_WB mem_wb_1 (
    .Clock(clock_8_out), .MemOut_in(mips_ram_1_p7), .ALU_result_in(ex_mem_1_alu_result_out),
    .MemOut_out(mem_wb_1_memout_out), .ALU_result_out(mem_wb_1_alu_result_out));
  Clock clock_8 (.out(clock_8_out));
  State state_3 (
    .Clock(clock_8_out), .RegWrite_in(rd_MEM), .MemToReg_in(state_2_memtoreg),
    .MemToReg_in_2(state_2_memtoreg_out), .RegWrite_out(rd_WB), .MemToReg(WriteEnable),
    .MemToReg_out(state_3_memtoreg_out), .MemToReg_in_7(state_2_memtoreg_out_5), .MemToReg_out_5(WriteTo_RA),
    .Clear(1'b0), .in_3(1'b0));  // open: MemToReg_in_3, MemToReg_2, MemToReg_in_4, MemToReg_out_2, MemToReg_in_5, MemToReg_out_3, RegWrite_in_2, RegWrite_out_2, MemToReg_in_6, MemToReg_out_4, MemToReg_in_8, MemToReg_out_6, RegWrite_in_3, RegWrite_out_3, RegWrite_in_4, RegWrite_out_4
  Multiplexer #(.width(32), .enable("false")) multiplexer_13 (
    .in0(mem_wb_1_memout_out), .in1(mem_wb_1_alu_result_out), .out(WBResult), .sel(state_3_memtoreg_out));
  // Probe on undriven

  // Other names for the same wires on the sheet: Clear = in_1; Flush_pipeline = out_2; RegAddress[4:0] = rd_WB;
  //   WriteData[31:0] = WBResult

  // Notes on the sheet:
  //   WB
  //   MEM
  //   EX
  //   ID
  //   IF
  //   PC
  //   Inst.
  //   IF/ID
  //   rt
  //   rs
  //   rt
  //   rs
  //   rs
  //   rt
  //   rs
  //   rt
  //   rt
  //   rs
  //   Write Dest
  //   DeleteMe
  //   Jump og jal skal i state
  //   ID/EX
  //   PC
  //   Immediate
  //   EX/MEM
  //   PC
  //   Register B
  //   ALU result
  //   MEM/WB
endmodule

module ALUOp (
  input  [2:0] ALUOp,
  input  [5:0] funct,
  output [3:0] ALU,
  output JUMP
);

  // PLA pla_1: pin names not known; wires that end beside it: {ALUOp, funct}
endmodule

module IF_ID (
  input  Clock,
  input  Clear,
  input  [31:0] PC_in,
  input  [31:0] Instruction_in,
  output [31:0] PC_out,
  output [31:0] Instruction_out
);

  Register #(.width(32), .trigger("low")) PC (.D(PC_in), .en(1'b1), .Q(PC_out), .clk(Clock), .clr(Clear));
  Register #(.width(32), .trigger("low")) Instruction (
    .D(Instruction_in), .en(1'b1), .Q(Instruction_out), .clk(Clock), .clr(Clear));
endmodule

module ID_EX (
  input  Clock,
  input  Clear,
  input  Disable_output,
  input  [31:0] PC_in,
  input  [31:0] Read_Data_1_in,
  input  [31:0] Read_Data_2_in,
  input  [31:0] Sign_Ext_in,
  input  [5:0] ALUOp_in,
  output [31:0] PC_out,
  output [31:0] Read_Data_1_out,
  output [31:0] Read_Data_2_out,
  output [31:0] Sign_Ext_out,
  output [5:0] ALUOp_out
);

  wire [5:0] ALUOp_q;
  wire [31:0] PC_q, Read_Data_1_q, Read_Data_2_q, Sign_Ext_q;

  Register #(.width(32), .trigger("falling")) PC (.D(PC_in), .en(1'b1), .Q(PC_q), .clk(Clock), .clr(Clear));
  Register #(.width(32), .trigger("falling")) Read_Data_1 (
    .D(Read_Data_1_in), .en(1'b1), .Q(Read_Data_1_q), .clk(Clock), .clr(Clear));
  Register #(.width(32), .trigger("falling")) Read_Data_2 (
    .D(Read_Data_2_in), .en(1'b1), .Q(Read_Data_2_q), .clk(Clock), .clr(Clear));
  Register #(.width(32), .trigger("falling")) Sign_Ext (
    .D(Sign_Ext_in), .en(1'b1), .Q(Sign_Ext_q), .clk(Clock), .clr(Clear));
  Register #(.width(6), .trigger("falling")) ALUOp (.D(ALUOp_in), .en(1'b1), .Q(ALUOp_q), .clk(Clock), .clr(Clear));
  Multiplexer #(.width(32), .enable("false")) multiplexer_1 (
    .in0(PC_q), .in1({32{1'b0}}), .out(PC_out), .sel(Disable_output));
  Multiplexer #(.width(32), .enable("false")) multiplexer_2 (
    .in0(Read_Data_1_q), .in1({32{1'b0}}), .out(Read_Data_1_out), .sel(Disable_output));
  Multiplexer #(.width(32), .enable("false")) multiplexer_3 (
    .in0(Read_Data_2_q), .in1({32{1'b0}}), .out(Read_Data_2_out), .sel(Disable_output));
  Multiplexer #(.width(32), .enable("false")) multiplexer_4 (
    .in0(Sign_Ext_q), .in1({32{1'b0}}), .out(Sign_Ext_out), .sel(Disable_output));
  Multiplexer #(.width(6), .enable("false")) multiplexer_5 (
    .in0(ALUOp_q), .in1({6{1'b0}}), .out(ALUOp_out), .sel(Disable_output));
endmodule

module EX_MEM (
  input  Clock,
  input  [31:0] PC_in,
  input  [31:0] ALU_result_in,
  input  [31:0] Read_Data_2,
  output [31:0] PC_out,
  output [31:0] ALU_result_out,
  output [31:0] Read_Data_2_2
);

  Register #(.width(32), .trigger("falling")) PC (.D(PC_in), .en(1'b1), .Q(PC_out), .clk(Clock), .clr(1'b0));
  Register #(.width(32), .trigger("falling")) ALU (
    .D(ALU_result_in), .en(1'b1), .Q(ALU_result_out), .clk(Clock), .clr(1'b0));
  Register #(.width(32), .trigger("falling")) u_Read_Data_2 (
    .D(Read_Data_2), .en(1'b1), .Q(Read_Data_2_2), .clk(Clock), .clr(1'b0));
endmodule

module MEM_WB (
  input  Clock,
  input  [31:0] MemOut_in,
  input  [31:0] ALU_result_in,
  output [31:0] MemOut_out,
  output [31:0] ALU_result_out
);

  Register #(.width(32), .trigger("falling")) MemOut (
    .D(MemOut_in), .en(1'b1), .Q(MemOut_out), .clk(Clock), .clr(1'b0));
  Register #(.width(32), .trigger("falling")) ALU (
    .D(ALU_result_in), .en(1'b1), .Q(ALU_result_out), .clk(Clock), .clr(1'b0));
endmodule

module State (
  input  Clock,
  input  Clear,
  input  in_3,
  input  [4:0] RegWrite_in,
  input  MemToReg_in,
  input  MemToReg_in_2,
  input  MemToReg_in_3,
  input  MemToReg_in_4,
  input  MemToReg_in_5,
  input  [2:0] RegWrite_in_2,
  input  MemToReg_in_6,
  input  MemToReg_in_7,
  input  [31:0] MemToReg_in_8,
  input  [4:0] RegWrite_in_3,
  input  [4:0] RegWrite_in_4,
  output [4:0] RegWrite_out,
  output MemToReg,
  output MemToReg_out,
  output MemToReg_2,
  output MemToReg_out_2,
  output MemToReg_out_3,
  output [2:0] RegWrite_out_2,
  output MemToReg_out_4,
  output MemToReg_out_5,
  output [31:0] MemToReg_out_6,
  output [4:0] RegWrite_out_3,
  output [4:0] RegWrite_out_4
);

  wire MemToReg_2_q, MemToReg_3_q, MemToReg_4_q, MemToReg_5_q, MemToReg_6_q, MemToReg_7_q, MemToReg_q;
  wire [2:0] RegWrite_2_q;
  wire [4:0] RegWrite_3_q, RegWrite_4_q, RegWrite_q;
  wire [31:0] MemToReg_8_q;

  Register #(.width(5), .trigger("falling")) RegWrite (
    .D(RegWrite_in), .en(1'b1), .Q(RegWrite_q), .clk(Clock), .clr(Clear));
  Register #(.width(1), .trigger("falling")) u_MemToReg (
    .D(MemToReg_in), .en(1'b1), .Q(MemToReg_q), .clk(Clock), .clr(Clear));
  Register #(.width(1), .trigger("falling")) u_MemToReg_2 (
    .D(MemToReg_in_2), .en(1'b1), .Q(MemToReg_2_q), .clk(Clock), .clr(Clear));
  Register #(.width(1), .trigger("falling")) MemToReg_3 (
    .D(MemToReg_in_3), .en(1'b1), .Q(MemToReg_3_q), .clk(Clock), .clr(Clear));
  Register #(.width(1), .trigger("falling")) MemToReg_4 (
    .D(MemToReg_in_4), .en(1'b1), .Q(MemToReg_4_q), .clk(Clock), .clr(Clear));
  Register #(.width(1), .trigger("falling")) MemToReg_5 (
    .D(MemToReg_in_5), .en(1'b1), .Q(MemToReg_5_q), .clk(Clock), .clr(Clear));
  Register #(.width(3), .trigger("falling")) RegWrite_2 (
    .D(RegWrite_in_2), .en(1'b1), .Q(RegWrite_2_q), .clk(Clock), .clr(Clear));
  Register #(.width(1), .trigger("falling")) MemToReg_6 (
    .D(MemToReg_in_6), .en(1'b1), .Q(MemToReg_6_q), .clk(Clock), .clr(Clear));
  Register #(.width(1), .trigger("falling")) MemToReg_7 (
    .D(MemToReg_in_7), .en(1'b1), .Q(MemToReg_7_q), .clk(Clock), .clr(Clear));
  Register #(.width(32), .trigger("falling")) MemToReg_8 (
    .D(MemToReg_in_8), .en(1'b1), .Q(MemToReg_8_q), .clk(Clock), .clr(Clear));
  Register #(.width(5), .trigger("falling")) RegWrite_3 (
    .D(RegWrite_in_3), .en(1'b1), .Q(RegWrite_3_q), .clk(Clock), .clr(Clear));
  Register #(.width(5), .trigger("falling")) RegWrite_4 (
    .D(RegWrite_in_4), .en(1'b1), .Q(RegWrite_4_q), .clk(Clock), .clr(Clear));
  Multiplexer #(.width(5), .enable("false")) multiplexer_1 (
    .in0(RegWrite_q), .in1({5{1'b0}}), .out(RegWrite_out), .sel(in_3));
  Multiplexer #(.enable("false")) multiplexer_2 (.in0(MemToReg_q), .in1(1'b0), .out(MemToReg), .sel(in_3));
  Multiplexer #(.enable("false")) multiplexer_3 (.in0(MemToReg_2_q), .in1(1'b0), .out(MemToReg_out), .sel(in_3));
  Multiplexer #(.enable("false")) multiplexer_4 (.in0(MemToReg_3_q), .in1(1'b0), .out(MemToReg_2), .sel(in_3));
  Multiplexer #(.enable("false")) multiplexer_5 (.in0(MemToReg_4_q), .in1(1'b0), .out(MemToReg_out_2), .sel(in_3));
  Multiplexer #(.enable("false")) multiplexer_6 (.in0(MemToReg_5_q), .in1(1'b0), .out(MemToReg_out_3), .sel(in_3));
  Multiplexer #(.width(3), .enable("false")) multiplexer_7 (
    .in0(RegWrite_2_q), .in1(3'b000), .out(RegWrite_out_2), .sel(in_3));
  Multiplexer #(.enable("false")) multiplexer_8 (.in0(MemToReg_6_q), .in1(1'b0), .out(MemToReg_out_4), .sel(in_3));
  Multiplexer #(.enable("false")) multiplexer_9 (.in0(MemToReg_7_q), .in1(1'b0), .out(MemToReg_out_5), .sel(in_3));
  Multiplexer #(.width(32), .enable("false")) multiplexer_10 (
    .in0(MemToReg_8_q), .in1({32{1'b0}}), .out(MemToReg_out_6), .sel(in_3));
  Multiplexer #(.width(5), .enable("false")) multiplexer_11 (
    .in0(RegWrite_3_q), .in1({5{1'b0}}), .out(RegWrite_out_3), .sel(in_3));
  Multiplexer #(.width(5), .enable("false")) multiplexer_12 (
    .in0(RegWrite_4_q), .in1({5{1'b0}}), .out(RegWrite_out_4), .sel(in_3));
endmodule

module Data_Hazard (
  input  [1:0] \type ,
  input  [4:0] rt,
  input  [4:0] rd,
  input  [4:0] rs,
  output Alert_rs,
  output Alert_rt
);

  wire mips_alu_1_p4, mips_alu_1_p5, mips_alu_2_p4, mips_alu_3_p4, not_1_out, or_1_out;
  wire [31:0] bit_extender_1_out, bit_extender_2_out, bit_extender_3_out;

  assign bit_extender_1_out = {{27{1'b0}}, rd};  // Bit_Extender bit_extender_1
  not not_1 (not_1_out, mips_alu_1_p4);
  // MIPS_ALU mips_alu_1: pin names not known; wires that end beside it: bit_extender_1_out, {32{1'b0}}, 4'b0010, mips_alu_1_p4, mips_alu_1_p5
  assign bit_extender_2_out = {{27{1'b0}}, rt};  // Bit_Extender bit_extender_2
  assign bit_extender_3_out = {{27{1'b0}}, rs};  // Bit_Extender bit_extender_3
  // MIPS_ALU mips_alu_2: pin names not known; wires that end beside it: bit_extender_2_out, mips_alu_1_p5, 4'b0110, mips_alu_2_p4
  // MIPS_ALU mips_alu_3: pin names not known; wires that end beside it: mips_alu_1_p5, bit_extender_3_out, 4'b0110, mips_alu_3_p4
  or or_1 (or_1_out, \type [0], \type [1]);
  and and_1 (Alert_rs, mips_alu_2_p4, not_1_out, \type [0]);
  and and_2 (Alert_rt, or_1_out, not_1_out, mips_alu_3_p4);

  // Notes on the sheet:
  //   Ignore if $zero
  //   (add)
  //   (Subu)
  //   (Subu)
endmodule

module Check_type (
  input  [5:0] OP,
  output [1:0] \type 
);

  // PLA pla_1: pin names not known; wires that end beside it: OP, \type 
endmodule

module Forwarding_unit (
  input  in_1,
  input  in_2,
  input  in_3,
  output [1:0] out_4
);

  // PLA pla_1: pin names not known; wires that end beside it: out_4
endmodule

module jal_PC (
  input  [31:0] in_1,
  input  [31:0] in_2,
  output [31:0] out_3
);

  wire [27:0] bit_extender_1_out;

  assign bit_extender_1_out = {{2{1'b0}}, in_1[25:0]};  // Bit_Extender bit_extender_1
  Shifter #(.width(28)) shifter_1 (.in(bit_extender_1_out), .\dist (5'b00010), .out(out_3[27:0]));

  assign out_3[31:28] = in_2[31:28];
endmodule

module Is_lw (
  input  [31:0] in_1,
  output \type 
);

  wire not_1_out, not_2_out, not_3_out;

  not not_1 (not_1_out, in_1[28]);
  not not_2 (not_2_out, in_1[29]);
  not not_3 (not_3_out, in_1[30]);
  and and_1 (\type , in_1[26], in_1[27], not_1_out, not_2_out, not_3_out, in_1[31]);

  // Notes on the sheet:
  //   Op
endmodule

module Wait_1_cycle (
  input  Trigger_stall,
  output out_2
);

  wire and_1_out, clock_1_out, d_ff_1_q, d_ff_1_qn, multiplexer_1_out, multiplexer_3_out, Stall_next_cycle_q,
       undriven;

  Multiplexer #(.enable("false")) multiplexer_1 (
    .in0(Trigger_stall), .in1(1'b0), .out(multiplexer_1_out), .sel(Stall_next_cycle_q));
  Register #(.width(1)) Stall_next_cycle (
    .D(multiplexer_1_out), .en(1'b1), .Q(Stall_next_cycle_q), .clk(clock_1_out));  // open: clr
  Clock clock_1 (.out(clock_1_out));
  D_Flip_Flop #(.trigger("falling")) d_ff_1 (
    .clk(undriven), .Q(d_ff_1_q), .Qn(d_ff_1_qn), .en(1'b1), .reset(1'b0));  // open: D, preset
  and and_1 (and_1_out, undriven, d_ff_1_q);
  Multiplexer #(.enable("false")) multiplexer_2 (.in0(d_ff_1_q), .in1(d_ff_1_qn), .sel(and_1_out));  // open: out
  Multiplexer #(.enable("false")) multiplexer_3 (
    .in0(Stall_next_cycle_q), .in1(1'b0), .out(multiplexer_3_out), .sel(out_2));
  Register #(.width(1)) Stall_next_cycle_2 (
    .D(multiplexer_3_out), .en(1'b1), .Q(out_2), .clk(clock_1_out));  // open: clr
endmodule
