// Logisim project Single Cycle.circ as structural Verilog: 2 circuits, main circuit main
module main (
  input  in_1,
  output out_2,
  output out_3
);

  wire ALUjump, ALUSrc, Branch, clock_1_out, clock_2_out, clock_3_out, jal, MemRead, MemtoReg, MemWrite,
       nand_1_out, not_1_out, not_2_out, not_3_out, RegDst, RegWrite;
  wire [2:0] ALUOp;
  wire [3:0] adder_1_p3_2, mips_alu_1_p3;
  wire [4:0] mipsprogramrom_1_p2_2, multiplexer_1_out, multiplexer_3_out;
  wire [20:0] mipsprogramrom_1_p2;
  wire [27:0] adder_1_p3, bit_extender_1_out, shifter_1_out;
  wire [31:0] bit_extender_2_out, mips_alu_1_p2, mips_alu_1_p5, mips_alu_2_p4, mips_ram_1_p5,
       multiplexer_2_out, multiplexer_4_out, multiplexer_6_out, multiplexer_7_out, multiplexer_8_out, PC_q,
       registerfile_1_p9, registerfile_1_p10, shifter_2_out;
  wire [31:26] mipsprogramrom_1_p2_3;

  Clock clock_1 (.out(clock_1_out));
  Register #(.width(32)) PC (.D(multiplexer_7_out), .Q(PC_q), .clk(clock_1_out), .clr(in_1));  // open: en
  // Adder adder_1: pin names not known; wires that end beside it: PC_q, 32'h4, {adder_1_p3_2, adder_1_p3}
  // MIPSProgramROM mipsprogramrom_1: pin names not known; wires that end beside it: PC_q, {mipsprogramrom_1_p2_3, mipsprogramrom_1_p2_2, mipsprogramrom_1_p2}
  // PLA Control: pin names not known; wires that end beside it: mipsprogramrom_1_p2_3
  Multiplexer #(.width(5), .enable("false")) multiplexer_1 (
    .in0(mipsprogramrom_1_p2[20:16]), .in1(mipsprogramrom_1_p2[15:11]), .out(multiplexer_1_out), .sel(RegDst));
  assign bit_extender_1_out = {{2{1'b0}}, {mipsprogramrom_1_p2_2, mipsprogramrom_1_p2}};  // Bit_Extender bit_extender_1
  not not_1 (not_1_out, jal);
  Multiplexer #(.width(32), .enable("false")) multiplexer_2 (
    .in0({adder_1_p3_2, adder_1_p3}), .in1(multiplexer_8_out), .out(multiplexer_2_out), .sel(not_1_out));
  Multiplexer #(.width(5), .enable("false")) multiplexer_3 (
    .in0({5{1'b1}}), .in1(multiplexer_1_out), .out(multiplexer_3_out), .sel(not_1_out));
  Clock clock_2 (.out(clock_2_out));
  Shifter #(.width(28)) shifter_1 (.in(bit_extender_1_out), .\dist (5'b00010), .out(shifter_1_out));
  assign bit_extender_2_out = {{16{1'b0}}, mipsprogramrom_1_p2[15:0]};  // Bit_Extender bit_extender_2
  // RegisterFile registerfile_1: pin names not known; wires that end beside it: bit_extender_1_out, multiplexer_2_out, clock_2_out, RegWrite, multiplexer_3_out, mipsprogramrom_1_p2_2, mipsprogramrom_1_p2[20:16], in_1, registerfile_1_p9, registerfile_1_p10, registerfile_1_p10
  Multiplexer #(.width(32), .enable("false")) multiplexer_4 (
    .in0({adder_1_p3_2, adder_1_p3}), .in1(registerfile_1_p9), .out(multiplexer_4_out), .sel(ALUjump));
  // MIPS_ALU mips_alu_1: pin names not known; wires that end beside it: registerfile_1_p9, mips_alu_1_p2, mips_alu_1_p3, out_2, mips_alu_1_p5, out_3, mips_alu_1_p5[23:0], registerfile_1_p10
  Multiplexer #(.width(32), .enable("false")) multiplexer_5 (
    .in0(registerfile_1_p10), .in1(bit_extender_2_out), .out(mips_alu_1_p2), .sel(ALUSrc));
  ALUOp u_ALUOp (.ALUOp(ALUOp), .funct(mipsprogramrom_1_p2[5:0]), .ALU(mips_alu_1_p3), .JUMP(ALUjump));
  Multiplexer #(.width(32), .enable("false")) multiplexer_6 (
    .in0({adder_1_p3_2, shifter_1_out}), .in1(multiplexer_4_out), .out(multiplexer_6_out), .sel(not_2_out));
  not not_2 (not_2_out, jal);
  Shifter #(.width(32)) shifter_2 (.in(bit_extender_2_out), .\dist (5'b00010), .out(shifter_2_out));
  nand nand_1 (nand_1_out, out_2, Branch);
  // MIPS_ALU mips_alu_2: pin names not known; wires that end beside it: shifter_2_out, multiplexer_6_out, 4'b0010, mips_alu_2_p4
  not not_3 (not_3_out, clock_3_out);
  Clock clock_3 (.out(clock_3_out));
  Multiplexer #(.width(32), .enable("false")) multiplexer_7 (
    .in0(mips_alu_2_p4), .in1(multiplexer_6_out), .out(multiplexer_7_out), .sel(nand_1_out));
  // MIPS_RAM mips_ram_1: pin names not known; wires that end beside it: MemWrite, MemRead, not_3_out, in_1, mips_ram_1_p5
  Multiplexer #(.width(32), .enable("false")) multiplexer_8 (
    .in0(mips_ram_1_p5), .in1(mips_alu_1_p5), .out(multiplexer_8_out), .sel(MemtoReg));
  // MIPSProgramROM mipsprogramrom_2: pin names not known

  // Other names for the same wires on the sheet: Clear = in_1

  // Notes on the sheet:
  //   DELETE ME
  //   add
endmodule

module ALUOp (
  input  [2:0] ALUOp,
  input  [5:0] funct,
  output [3:0] ALU,
  output JUMP
);

  // PLA pla_1: pin names not known; wires that end beside it: {ALUOp, funct}
endmodule
